# Fritzing sketch Robot de pelea (saved by Fritzing 0.9.3b)

parts:
  Componente1 = Arduino Uno (Rev3)
  M1 = ps2 gamepad [package=THT]
  M2 = DC Motor
  M4 = DC Motor
  BAT1 = 12 battery [package=battery]
  JP1 = Header 8 [package=1x08_smd]
  RELAY2 = CAR RELAY [part_number=NVF4-2 package=THT]
  RELAY5 = CAR RELAY [part_number=NVF4-2 package=THT]
  RELAY6 = CAR RELAY [part_number=NVF4-2 package=THT]
  RELAY9 = CAR RELAY [part_number=NVF4-2 package=THT]
  VCC2 = 4 x AAA Battery Mount
  RELAY10 = CAR RELAY [part_number=NVF4-2 package=THT]
  M5 = DC Motor
  RELAY1 = CAR RELAY [part_number=NVF4-2 package=THT]
  A1 = 8-channel Power Relay

nets:
  N1: Componente1.D10_PWM/SS, M1.DAT, JP1.1
  N2: Componente1.D11_PWM/MOSI, M1.CMD, JP1.2
  N3: Componente1.D12/MISO, M1.CLK, JP1.7
  N4: Componente1.D13/SCK, M1.ATT, JP1.6
  GND: Componente1.GND, M1.GND, BAT1.-, JP1.4, RELAY2.86, RELAY5.86, RELAY6.86, RELAY9.86, VCC2.-, RELAY10.86, RELAY1.86, A1.GND
  N5: Componente1.D2, A1.IN1
  N6: Componente1.D3_PWM, A1.IN2
  N7: Componente1.D4, A1.IN3
  N8: Componente1.D5_PWM, A1.IN4
  N9: Componente1.D6_PWM, A1.IN5
  N10: Componente1.D7, A1.IN6
  3V3: Componente1.3V3, M1.3.3V, JP1.5
  5V: Componente1.5V, BAT1.+, VCC2.+, A1.VCC
  N11: M2.pin_1, RELAY1.30
  N12: M2.pin_2, RELAY2.30
  N13: M4.pin_1, RELAY9.30
  N14: M4.pin_2, RELAY10.30
  N15: RELAY2.87A, RELAY1.87A
  N16: RELAY2.85, A1.NO#31
  N17: RELAY2.87, RELAY1.87
  N18: RELAY5.87A, RELAY6.87A
  N19: RELAY5.85, A1.NO#28
  N20: RELAY5.30, M5.pin_1
  N21: RELAY5.87, RELAY6.87
  N22: RELAY6.85, A1.NO#25
  N23: RELAY6.30, M5.pin_2
  N24: RELAY9.87A, RELAY10.87A
  N25: RELAY9.85, A1.NO#22
  N26: RELAY9.87, RELAY10.87
  N27: RELAY10.85, A1.NO#19
  N28: RELAY1.85, A1.NO#34

custom parts:
  ps2 gamepad: PS2 gamepad. Warning! PCB view is designed for the female connector available from https://www.robotshop.com/en/ps2-connector.html. However there is no mechanical information that I can find so ipcb was generated from a scaled jpg and may well be wrong. Print the footprint out and check it against a real part before ordering boards!
  12 battery: 12V lead acid type battery, like the Husqvarna YTH2448 12V 35AH battery. This is the mini version 1/4 the size of the actual battery to be closer to typical breadboard parts (around 2in wide rathher than 7in). The pads in pcb are sized to accomidate up to 14ga wire (as these batterys will deliver high currents.)
